# Fritzing sketch thermistor_v2 (saved by Fritzing 0.9.3b)
breadboards: 1

parts:
  R3 = Resistor [tolerance=±5% resistance=1k package=THT]
  R4 = Temperature Sensor (Thermistor) [thermistor_type=NTC package=THT]
  Part1 = Arduino Uno (Rev3)

nets:
  N1: R3.Pin_0, Part1.AREF, Part1.5V
  N2: R3.Pin_1, R4.pin_0, Part1.A1
